# Fritzing sketch SKEMATIK BETTER ONE (saved by Fritzing 0.9.2b)

parts:
  Part1 = Arduino Uno (Rev3)
  VCC1 = Battery block 9V
  M1 = sim800L v2 evb

nets:
  N1: Part1.D9_PWM, M1.pin_3
  N2: Part1.D10_PWM/SS, M1.pin_4
  N3: Part1.GND, VCC1.-, M1.pin_2, M1.pin_6
  N4: Part1.5V, M1.pin_7
  N5: Part1.VIN, VCC1.+

custom parts:
  sim800L v2 evb: sim800L v2 evb GSM module.
