# Fritzing sketch SKEMATIK FOR NOW (saved by Fritzing 0.9.2b)
breadboards: 1

parts:
  Part1 = Arduino Uno (Rev3) - ICSP
  U2 = SUP500F [package=sup500f]
  Part2 = Adafruit FONA - Mini Cellular GSM Breakout
  Part3 = Triple Axis Accelerometer Breakout - ADXL345  # not connected

nets:
  N1: Part1.D9_PWM, Part2.TXD_5V, Part2.RI_5V
  N2: Part1.D10_PWM/SS, Part2.RXD_5V
  N3: Part1.D3_PWM, U2.TX-O
  N4: Part1.D4, U2.GND
  5V: Part1.5V, U2.VCC
  N5: Part1.GND, U2.RX-I

custom parts:
  Adafruit FONA - Mini Cellular GSM Breakout: An all-in-one cellular phone module that lets you add voice, text, SMS and GPRS data to your project. Quad-band 850/900/1800/1900MHz - connect onto any global GSM network with any 2G SIM. Includes an onboard LiPoly battery charging circuitry so you can take your project on the go. Also works as an FM radio receiver.
